# Fritzing sketch Diecast_2_BT_RCSchematic_with_lights (saved by Fritzing 0.9.3b)
breadboards: 1

parts:
  Part1 = Arduino Nano (Rev3.0)
  Part2 = Bluetooth HC-05 Macho
  R1 = Resistor [tolerance=±5% resistance=1k package=THT]
  R2 = Resistor [tolerance=±5% resistance=2k package=THT]
  U1 = LIPO-1000mAh [package=lipo-1000]
  U2 = LIPO-1000mAh [package=lipo-1000]
  Steering = Basic Servo
  Car_engine = Basic Servo
  IC1 = Voltage Regulator LM1117 [package=sot223]
  IC3 = Voltage Regulator LM1117 [package=sot223]
  C1 = Electrolytic Capacitor [capacitance=1µF package="100 mil [THT, electrolytic]"]
  C3 = Electrolytic Capacitor [capacitance=1µF package="100 mil [THT, electrolytic]"]
  C4 = Electrolytic Capacitor [capacitance=1µF package="100 mil [THT, electrolytic]"]
  LED1 = smd LED [color="Red (633nm)" package="0805 [SMD]"]
  LED2 = smd LED [color="Red (633nm)" package="0805 [SMD]"]
  LED3 = smd LED [color="Red (633nm)" package="0805 [SMD]"]
  LED4 = smd LED [color="Red (633nm)" package="0805 [SMD]"]
  headlight_left = LEDs [package=led10mm]
  headlight_right = LEDs [package=led10mm]
  Car_Horn = Piezo Speaker
  IC4 = Voltage Regulator LM1117 [package=sot223]
  C5 = Electrolytic Capacitor [capacitance=1µF package="100 mil [THT, electrolytic]"]

nets:
  GND: Part1.GND, Part2.GND, R2.Pin_0, U2.-, Steering.gnd, Car_engine.gnd, IC1.ADJ, IC3.ADJ, C1.-, C3.-, C4.-, IC4.ADJ, C5.-
  N1: Part1.D2, R1.Pin_1
  N2: Part1.D3, Part2.TXD
  N3: Part1.D5, Steering.pulse
  N4: Part1.D6, Car_engine.pulse
  N5: Part1.D7, LED2.cathode
  N6: Part1.D8, LED3.cathode
  N7: Part1.D9, headlight_left.C, headlight_right.A
  N8: Part1.D10, Car_Horn.pin1
  N9: Part1.VIN, U1.+, IC1.IN, IC3.IN, C4.+, IC4.IN
  5V: Part1.5V, Part2.VCC, LED1.anode, LED4.anode, headlight_left.A, headlight_right.C
  N10: Part2.RXD, R1.Pin_0, R2.Pin_1
  N11: U1.-, U2.+
  N12: Steering.vcc, IC1.OUT, C3.+
  N13: Car_engine.vcc, IC3.OUT, C1.+
  N14: LED1.cathode, LED2.anode
  N15: LED3.anode, LED4.cathode
  N16: Car_Horn.pin2, IC4.OUT, C5.+
