# Fritzing sketch Diecast_2_BT_RC_Schematic (saved by Fritzing 0.9.3b)
breadboards: 1

parts:
  Part1 = Arduino Nano (Rev3.0)
  Part2 = Bluetooth HC-05 Macho
  R1 = Resistor [tolerance=±5% resistance=1k package=THT]
  R2 = Resistor [tolerance=±5% resistance=2k package=THT]
  U1 = LIPO-1000mAh [package=lipo-1000]
  U2 = LIPO-1000mAh [package=lipo-1000]
  Steering = Basic Servo
  Car_engine = Basic Servo
  IC1 = Voltage Regulator LM1117 [package=sot223]
  IC2 = Voltage Regulator LM1117 [package=sot223]
  IC3 = Voltage Regulator LM1117 [package=sot223]
  C1 = Electrolytic Capacitor [capacitance=1µF package="100 mil [THT, electrolytic]"]
  C2 = Electrolytic Capacitor [capacitance=1µF package="100 mil [THT, electrolytic]"]
  C3 = Electrolytic Capacitor [capacitance=1µF package="100 mil [THT, electrolytic]"]
  C4 = Electrolytic Capacitor [capacitance=1µF package="100 mil [THT, electrolytic]"]

nets:
  GND: Part1.GND, Part2.GND, R2.Pin_0, U2.-, Steering.gnd, Car_engine.gnd, IC1.ADJ, IC2.ADJ, IC3.ADJ, C1.-, C2.-, C3.-, C4.-
  N1: Part1.D2, Steering.pulse
  N2: Part1.D3, Car_engine.pulse
  N3: Part1.D4, Part2.TXD
  N4: Part1.D5, R1.Pin_1
  VIN: Part1.VIN, Part2.VCC, IC2.OUT, C2.+
  N5: Part2.RXD, R1.Pin_0, R2.Pin_1
  N6: U1.+, IC1.IN, IC2.IN, IC3.IN, C4.+
  N7: U1.-, U2.+
  N8: Steering.vcc, IC1.OUT, C3.+
  N9: Car_engine.vcc, IC3.OUT, C1.+
